// Logisim project TTY_Controller.circ as structural Verilog: 2 circuits, main circuit controller
module controller (
  input  [31:0] Addr_From_CPU,
  input  [31:0] Data_From_CPU,
  input  En_Read,
  input  DMA_ACK,
  output [31:0] Addr_To_CPU,
  output [31:0] Data_To_CPU,
  output En_Write,
  output DMA_REQ
);
endmodule

module ECAMs (
);

  wire [31:26] undriven;

  Comparator #(.mode("unsigned"), .width(6)) comparator_1 (.a(undriven), .b(6'b111000));  // open: gt, eq, lt
  // Common_ECAM common_ecam_1: pin names not known

  // Notes on the sheet:
  //   ECAM
endmodule
