// Logisim project Main_Memories.circ as structural Verilog: 2 circuits, main circuit Memory
module Memory (
  input  [31:0] Addr,
  input  RST,
  input  Read_En,
  input  [7:0] Write_Flags,
  input  Clk,
  input  [31:0] Data_In,
  input  Write_En,
  output RAM_Ready,
  output [63:0] out_9
);

  wire decoder_1_out0, decoder_1_out1, decoder_1_out2, decoder_1_out3;
  wire [7:0] ram_1_p5, ram_1_p6, ram_1_p7, ram_1_p8, ram_1_p9, ram_1_p10, ram_1_p11, ram_1_p12, ram_2_p5,
       ram_3_p5, ram_3_p6, ram_3_p7, ram_3_p8, ram_3_p9, ram_3_p10, ram_3_p11, ram_3_p12, ram_4_p5, ram_4_p6,
       ram_4_p7, ram_4_p8, ram_4_p9, ram_4_p10, ram_4_p11, ram_4_p12, undriven, undriven_2, undriven_3,
       undriven_4, undriven_5, undriven_6, undriven_7;

  Decoder #(.select(2)) decoder_1 (
    .out0(decoder_1_out0), .out1(decoder_1_out1), .out2(decoder_1_out2), .out3(decoder_1_out3),
    .sel(Addr[31:30]), .en(Write_En));
  // RAM #(.addrWidth(30), .clearpin("true"), .enables("line"), .line("octo"), .misaligned("true")) ram_1: pin names not known; wires that end beside it: Addr[29:0], decoder_1_out3, Clk, RST, ram_1_p5, ram_1_p6, ram_1_p7, ram_1_p8, ram_1_p9, ram_1_p10, ram_1_p11, ram_1_p12
  // RAM #(.addrWidth(30), .clearpin("true"), .enables("line"), .line("octo"), .misaligned("true")) ram_2: pin names not known; wires that end beside it: Addr[29:0], decoder_1_out0, Clk, RST, ram_2_p5
  // RAM #(.addrWidth(30), .clearpin("true"), .enables("line"), .line("octo"), .misaligned("true")) ram_3: pin names not known; wires that end beside it: Addr[29:0], decoder_1_out1, Clk, RST, ram_3_p5, ram_3_p6, ram_3_p7, ram_3_p8, ram_3_p9, ram_3_p10, ram_3_p11, ram_3_p12
  // RAM #(.addrWidth(30), .clearpin("true"), .enables("line"), .line("octo"), .misaligned("true")) ram_4: pin names not known; wires that end beside it: Addr[29:0], decoder_1_out2, Clk, RST, ram_4_p5, ram_4_p6, ram_4_p7, ram_4_p8, ram_4_p9, ram_4_p10, ram_4_p11, ram_4_p12
  Multiplexer #(.enable("true"), .select(2), .width(64)) multiplexer_1 (
    .in0({ram_3_p11, ram_3_p10, ram_3_p9, ram_3_p8, ram_3_p7, ram_3_p6, ram_3_p5, ram_2_p5}),
    .in1({ram_4_p11, ram_4_p10, ram_4_p9, ram_4_p8, ram_4_p7, ram_4_p6, ram_4_p5, ram_3_p12}),
    .in2({undriven_7, undriven_6, undriven_5, undriven_4, undriven_3, undriven_2, undriven, ram_4_p12}),
    .in3({ram_1_p12, ram_1_p11, ram_1_p10, ram_1_p9, ram_1_p8, ram_1_p7, ram_1_p6, ram_1_p5}), .out(out_9),
    .sel(Addr[31:30]), .en(Read_En));

  assign RAM_Ready = 1'b1;

  // Other names for the same wires on the sheet: Sel[1:0] = Addr[31:30]
endmodule

module ROM_BIOS (
  input  [19:0] Addr,
  output [63:0] Data_Out
);

  // ROM #(.addrWidth(20), .line("octo"), .misaligned("true")) rom_1: pin names not known; wires that end beside it: Addr, Data_Out[31:24], Data_Out[23:16], Data_Out[15:8], Data_Out[7:0], Data_Out[63:56], Data_Out[55:48], Data_Out[47:40], Data_Out[39:32]

  // Notes on the sheet:
  //   contents of rom_1 (hex, n*v repeats v):
  //   8c f0 ff f0 8d f0 0 14 e f 0 0 14 7a 0 0 1 0 0 0 8c 10 ff f0 8d 10 0 c 15 1c 0 0 8c f0 ff f0 8d f0 0
  //   64 10 f 0 0 8c 10 0 0 8d 10 10 0 15 14 0 0 c 10 0 1 15 13 0 0 c 10 0 3 15 16 0 0 8c f0 ff f0 8d f0 0
  //   b4 10 f 0 0 8c f0 ff f0 8d f0 0 c8 10 f 0 0 1 0 0 0 8c 10 0 0 8d 10 10 0 8c 20 0 0 8d 20 20 1 53 12
  //   0 0 8c 20 0 0 8d 20 30 1 53 12 f fc 8c 10 0 0 8d 10 20 0 8c 20 0 0 8d 20 50 1 53 12 0 14 8c 20 0 0
  //   8d 20 60 3 53 12 0 18 8c 20 0 0 8d 20 0 1 53 12 0 0 11 0 0 0 8c 10 0 0 8d 10 50 0 c 20 99 99 53 12 0
  //   0 11 0 0 0 8c 10 0 0 8d 10 60 0 c 20 de ad 53 12 0 0 11 1048343*0 8c f0 ff f0 8d f0 0 0 e f
endmodule
