// Logisim project mother.circ as structural Verilog: 2 circuits, main circuit main
module main (
  input  in_1,
  input  in_2
);

  wire die_1_clk_out, die_1_dma_ack_2, die_1_en_read_to_perif_2, die_1_hlt, die_1_read_en, die_1_rst_out,
       die_1_write_en, memory_1_ram_ready, on_off_sys_1_clk_out, on_off_sys_1_rst_out, undriven_3, undriven_4;
  wire [7:0] die_1_write_flags;
  wire [19:0] die_1_rom_addr;
  wire [31:0] die_1_addr, die_1_addr_to_perif_2, die_1_data_out, die_1_data_to_perif_2, undriven, undriven_2;
  wire [63:0] memory_1_out_9, rom_bios_1_data_out;

  LED led_1 (.in(die_1_hlt));
  On_Off_Sys on_off_sys_1 (.RST(in_2), .Clk(in_1), .RST_Out(on_off_sys_1_rst_out), .Clk_Out(on_off_sys_1_clk_out));
  ROM_BIOS rom_bios_1 (.Addr(die_1_rom_addr), .Data_Out(rom_bios_1_data_out));
  Die die_1 (
    .Addr_From_Perif_2(undriven), .Data_From_Perif_2(undriven_2), .En_Write_2(undriven_3),
    .DMA_REQ_2(undriven_4), .ROM_Data_In(rom_bios_1_data_out), .RAM_Ready(memory_1_ram_ready),
    .Clk(on_off_sys_1_clk_out), .RST(on_off_sys_1_rst_out), .Data_In(memory_1_out_9),
    .RST_Out(die_1_rst_out), .Addr_To_Perif_2(die_1_addr_to_perif_2),
    .Data_To_Perif_2(die_1_data_to_perif_2), .En_Read_To_Perif_2(die_1_en_read_to_perif_2),
    .DMA_ACK_2(die_1_dma_ack_2), .ROM_Addr(die_1_rom_addr), .Clk_Out(die_1_clk_out), .Read_En(die_1_read_en),
    .Write_En(die_1_write_en), .HLT(die_1_hlt), .Write_Flags(die_1_write_flags), .Addr(die_1_addr),
    .Data_Out(die_1_data_out));  // open: Addr_From_Perif_1, Data_From_Perif_1, En_Write_1, DMA_REQ_1, Addr_From_Perif_3, Data_From_Perif_3, En_Write_3, DMA_REQ_3, Addr_To_Perif_1, Data_To_Perif_1, En_Read_To_Perif_1, DMA_ACK_1, Addr_To_Perif_3, Data_To_Perif_3, En_Read_To_Perif_3, DMA_ACK_3
  // Probe on rom_bios_1_data_out
  // Probe on die_1_rom_addr
  Memory memory_1 (
    .Write_En(die_1_write_en), .RST(die_1_rst_out), .Read_En(die_1_read_en), .Write_Flags(die_1_write_flags),
    .Clk(die_1_clk_out), .Data_In(die_1_data_out), .Addr(die_1_addr), .RAM_Ready(memory_1_ram_ready),
    .out_9(memory_1_out_9));
  // Probe on die_1_data_out
  // Probe on memory_1_out_9
  // Probe on die_1_addr
  // Probe on die_1_addr_to_perif_2
  // Probe on undriven
  // Probe on die_1_data_to_perif_2
  // Probe on undriven_2
  // Probe on undriven_3
  // Probe on undriven_4
  // Probe on die_1_en_read_to_perif_2
  // Probe on die_1_dma_ack_2
endmodule

module On_Off_Sys (
  input  RST,
  input  Clk,
  output RST_Out,
  output Clk_Out
);

  wire and_1_out, and_2_out, and_3_out, and_4_out, and_5_out, and_6_out, and_7_out, and_8_out, and_9_out,
       and_10_out, and_11_out, and_12_out, and_13_out, or_1_out, or_2_out, or_3_out, or_4_out, Q0, Q1, Q2;

  and and_1 (and_1_out, ~Q1, RST);  // AND_Gate
  and and_2 (and_2_out, ~Q1, Q0);  // AND_Gate
  and and_3 (and_3_out, Q0, RST);
  and and_4 (and_4_out, ~Q0, Q2);  // AND_Gate
  and and_5 (and_5_out, ~Q2, Q0);  // AND_Gate
  and and_6 (and_6_out, Q1, ~Q0);  // AND_Gate
  and and_7 (and_7_out, Q1, RST);
  and and_8 (and_8_out, Q2, ~Q0);  // AND_Gate
  and and_9 (and_9_out, Q2, RST);
  and and_10 (and_10_out, Q1, ~Q0, RST);  // AND_Gate
  or or_1 (or_1_out, and_1_out, and_2_out, and_3_out, and_4_out);
  or or_2 (or_2_out, and_5_out, and_6_out, and_7_out);
  or or_3 (or_3_out, and_8_out, and_9_out, and_10_out);
  D_Flip_Flop d_ff_1 (.D(or_1_out), .clk(Clk), .Q(Q0));  // open: Qn, preset, reset
  D_Flip_Flop d_ff_2 (.D(or_2_out), .clk(Clk), .Q(Q1));  // open: Qn, preset, reset
  D_Flip_Flop d_ff_3 (.D(or_3_out), .clk(Clk), .Q(Q2));  // open: Qn, preset, reset
  and and_11 (and_11_out, Q2, Q1, ~Q0);  // AND_Gate
  and and_12 (and_12_out, ~Q2, ~Q1, Q0);  // AND_Gate
  or or_4 (or_4_out, Q0, Q1);
  or or_5 (RST_Out, and_11_out, and_12_out);
  and and_13 (and_13_out, ~Q2, or_4_out);  // AND_Gate
  and and_14 (Clk_Out, and_13_out, Clk);
endmodule
